// Logisim project Reception_Desk.circ as structural Verilog: 5 circuits, main circuit main
module main (
  input  X,
  input  Y,
  input  ENABLE,
  output DOCTOR_A,
  output DOCTOR_B,
  output out_6
);

  wire clock_1_out, doctor_alloter_1_p3, doctor_alloter_1_p6, doctor_alloter_1_p7, doctor_alloter_1_p8;

  // doctor_alloter doctor_alloter_1: pin names not known; wires that end beside it: X, Y, doctor_alloter_1_p3, doctor_alloter_1_p3, ENABLE, doctor_alloter_1_p6, doctor_alloter_1_p7, doctor_alloter_1_p8, doctor_alloter_1_p6, doctor_alloter_1_p6
  Clock clock_1 (.out(clock_1_out));
  doctor_availabilty doctor_availabilty_1 (
    .A(DOCTOR_A), .B(DOCTOR_A), .Enable(DOCTOR_A), .Clock(DOCTOR_A), .BU(doctor_alloter_1_p3),
    .AU(doctor_alloter_1_p3), .AS(doctor_alloter_1_p3), .BS(doctor_alloter_1_p3), .out_9(doctor_alloter_1_p3));

  // Notes on the sheet:
  //   Doctor Alloter Part
  //   Clock for Needed Time
  //   Doctor Availability Part
  //   WAIT SIGNAL
endmodule

module doctor_alloter (
  input  X,
  input  Y,
  input  AU,
  input  BU,
  input  ENABLE,
  output A,
  output B,
  output ENABLE_2
);

  wire and_1_out, and_2_out, and_3_out, not_1_out, not_2_out, not_3_out, not_4_out, or_1_out, or_2_out;

  not not_1 (not_1_out, X);
  not not_2 (not_2_out, Y);
  not not_3 (not_3_out, AU);
  not not_4 (not_4_out, BU);
  or or_1 (or_1_out, not_1_out, not_2_out);
  and and_1 (and_1_out, Y, AU);
  and and_2 (and_2_out, AU, X);
  and and_3 (and_3_out, Y, X);
  and and_4 (A, or_1_out, ENABLE, not_3_out);
  or or_2 (or_2_out, and_2_out, and_1_out, and_3_out);
  buf and_5 (B, ENABLE);  // AND_Gate

  assign ENABLE_2 = ENABLE;

  // Notes on the sheet:
  //   Input Information
  //   X and Y are the inputs by user
  //   AU and BU are status inputs given by doctor_availability
  //   Doctor Alloter
  //   Output Information
  //   A and B return which doctor is alloted
endmodule

module doctor_availabilty (
  input  A,
  input  B,
  input  Enable,
  input  Clock,
  output BU,
  output AU,
  output AS,
  output BS,
  output out_9
);

  wire and_2_out, and_3_out, not_1_out, not_2_out;

  not not_1 (not_1_out, A);
  not not_2 (not_2_out, B);
  and and_1 (out_9, not_1_out, not_2_out);
  and and_2 (and_2_out, not_2_out, A);
  and and_3 (and_3_out, B, not_1_out);
  timer timer_1 (.Signal(and_2_out), .Enable(Enable), .Clock(Clock), .Feedback(AU), .Status(AS));
  timer timer_2 (.Signal(and_3_out), .Enable(Enable), .Clock(Clock), .Feedback(BU), .Status(BS));

  // Notes on the sheet:
  //   INPUT EXPLANATION:
  //   A and B is input which reprsents the doctor alloted by doctor_alloter
  //   A
  //   During the consultation , the status of doctor availiability is kept occupied for 15 seconds
  //   Any.enable is turned on, BU/AU checks and updates the status of respective doctors
  //   Doctor Availability Status Update
  //   Output explanation:
  //   The doctor status turns to 1
  //   Doctor status is further given as feedback and becomes input for doctor_alloter
  //   WAIT REQUEST
  //   DOCTOR B STATUS UPDATE
  //   DOCTOR A STATUS UPDATE
  //   DOCTOR A STATUS
  //   DOCTOR B STATUS
endmodule

module timer (
  input  Signal,
  input  Enable,
  input  Clock,
  output Feedback,
  output Status
);

  wire counter_1_carry_is_1_when_counter_finishes, not_1_out, not_2_out, s_r_ff_1_q;

  S_R_Flip_Flop s_r_ff_1 (
    .S(Signal), .clk(Clock), .R(1'b0), .Q(s_r_ff_1_q), .reset(counter_1_carry_is_1_when_counter_finishes));  // open: Qn, preset, en
  counter counter_1 (
    .Carry_is_1_when_counter_finishes(counter_1_carry_is_1_when_counter_finishes), .Clock(Clock),
    .Reset(not_2_out));
  not not_1 (not_1_out, counter_1_carry_is_1_when_counter_finishes);
  not not_2 (not_2_out, s_r_ff_1_q);
  and and_1 (Status, s_r_ff_1_q, not_1_out);
  D_Flip_Flop d_ff_1 (.clk(Enable), .D(Status), .Q(Feedback));  // open: Qn, preset, en, reset

  // Notes on the sheet:
  //   Timer
  //   A circuit that combines the use of flip flop and counter to give status and feedback of doctors
endmodule

module counter (
  input  Clock,
  input  Reset,
  output Carry_is_1_when_counter_finishes
);

  wire and_1_out, not_1_out;
  wire [3:0] t_ff_1_q;

  and and_1 (and_1_out, not_1_out, Clock);
  not not_1 (not_1_out, Carry_is_1_when_counter_finishes);
  T_Flip_Flop t_ff_1 (.clk(and_1_out), .T(1'b1), .Q(t_ff_1_q[0]), .reset(Reset), .en(1'b1));  // open: Qn, preset
  and and_2 (Carry_is_1_when_counter_finishes, t_ff_1_q[3], t_ff_1_q[2], t_ff_1_q[1]);
  T_Flip_Flop #(.trigger("falling")) t_ff_2 (
    .clk(t_ff_1_q[0]), .T(1'b1), .Q(t_ff_1_q[1]), .reset(Reset), .en(1'b1));  // open: Qn, preset
  T_Flip_Flop #(.trigger("falling")) t_ff_3 (
    .clk(t_ff_1_q[1]), .T(1'b1), .Q(t_ff_1_q[2]), .reset(Reset), .en(1'b1));  // open: Qn, preset
  // Probe on t_ff_1_q
  T_Flip_Flop #(.trigger("falling")) t_ff_4 (
    .clk(t_ff_1_q[2]), .T(1'b1), .Q(t_ff_1_q[3]), .reset(Reset), .en(1'b1));  // open: Qn, preset

  // Notes on the sheet:
  //   A counter circuit that returns 1 and stops counting as soon as it reaches the 0xD
  //   4-Bit Up Counter
endmodule
